# Fritzing sketch LCDJava (saved by Fritzing 0.9.3b)
circuit board: 8.46667cm x 5.64444cm
breadboards: 1

parts:
  Onderdeel1 = Arduino Uno (Rev3)
  LCM1602_IIC1 = LCM1602 IIC [part_number="LCM1602 IIC" chip_label="LCM1602 IIC" package="DIP (Dual Inline) [THT]"]
  LCD1 = LCD screen
  J1 = Piezo Speaker
  R1 = Resistor [tolerance=±5% resistance=220 package="2512 [SMD]"]
  T1 = LM35 Temperature Sensor [package="TO92 [THT]"]
  S1 = Pushbutton [package="[THT]"]
  S2 = Pushbutton [package="[THT]"]
  R2 = Resistor [tolerance=±5% resistance=220 package="2512 [SMD]"]
  R3 = Resistor [tolerance=±5% resistance=220 package="2512 [SMD]"]

nets:
  N1: Onderdeel1.A0, T1.Vout
  N2: Onderdeel1.A4/SDA, LCM1602_IIC1.SDA
  N3: Onderdeel1.A5/SCL, LCM1602_IIC1.SCL
  N4: Onderdeel1.D8, R1.Pin_0
  N5: Onderdeel1.D2, S1.Pin_1, S1.Pin_2, R3.Pin_0
  N6: Onderdeel1.D3_PWM, S2.Pin_1, S2.Pin_2, R2.Pin_0
  5V: Onderdeel1.5V, LCM1602_IIC1.VCC, T1.+Vs, S1.Pin_3, S1.Pin_4, S2.Pin_3, S2.Pin_4
  GND: Onderdeel1.GND, LCM1602_IIC1.GND, J1.pin1, T1.GND, R2.Pin_1, R3.Pin_1
  VSS: LCM1602_IIC1.VSS, LCD1.VSS
  VDD: LCM1602_IIC1.VDD, LCD1.VDD
  N7: LCM1602_IIC1.V0, LCD1.V0
  N8: LCM1602_IIC1.RS, LCD1.RS
  N9: LCM1602_IIC1.RW, LCD1.R/W
  N10: LCM1602_IIC1.E, LCD1.E
  N11: LCM1602_IIC1.D0, LCD1.DB0
  N12: LCM1602_IIC1.D1, LCD1.DB1
  N13: LCM1602_IIC1.D2, LCD1.DB2
  N14: LCM1602_IIC1.D3, LCD1.DB3
  N15: LCM1602_IIC1.D4, LCD1.DB4
  N16: LCM1602_IIC1.D5, LCD1.DB5
  N17: LCM1602_IIC1.D6, LCD1.DB6
  N18: LCM1602_IIC1.D7, LCD1.DB7
  N19: LCM1602_IIC1.A, LCD1.LED+
  N20: LCM1602_IIC1.K, LCD1.LED-
  N21: LCM1602_IIC1.LED_A, LCM1602_IIC1.LED_B
  N22: J1.pin2, R1.Pin_1

custom parts:
  LCM1602 IIC: I2C-Module to use a 1602 or 2004 LCD on with the wire.h libory Serial LCD Modul

// code stored in the sketch: AnalogReadSerial2LCD_LED.ino
#include <Wire.h>
#include <LiquidCrystal_I2C.h>

LiquidCrystal_I2C lcd(0x27, 16, 2);   // adress and format LCD

const int analogInPin = A0;           // Analog input pin that the potentiometer is attached to
const int analogOutPin = 9;           // Analog output pin that the LED is attached to

int sensorValue = 0;                  // value read from the pot
int outputValue = 0;                  // value output to the PWM (analog out)

void setup() {
  lcd.init();                         // init LCD
  lcd.backlight();
  lcd.home();
  lcd.setCursor(5, 0);                // place static text
  lcd.print("ADC = ");
  lcd.setCursor(15, 0);
  lcd.print("V");
  lcd.setCursor(0, 1);
  lcd.print("LED : ");
  lcd.setCursor(12, 1);
  lcd.print("%");
  Serial.begin(9600);                 // optional serial monitor
}

void loop() {
  int sensorValue = analogRead(analogInPin);          // read analog A0 en store in sensorValue
  float voltValue = 5.0 / 1024.0 * sensorValue;       // calculate volt at analog A0 and store in voltValue
  float percentValue = sensorValue / 1024.0 * 100.0;  // calculate percentage analog A0 and store in percentValue
  outputValue = map(sensorValue, 0, 1023, 0, 255);    // map analog input to analog output and store in outputValue
  analogWrite(analogOutPin, outputValue);             // write outputValue to analogOutPin

  lcd.setCursor(0, 0);                                // set cursor at deserid position
  leadingZeros(sensorValue, 4);                       // print sensorvalue with number of leading-characters (0 or space as specified in function leadingZeros)
  lcd.setCursor(10, 0);                               // set cursor at deserid position
  lcd.print(voltValue);                               // print voltValue
  lcd.setCursor(6, 1);                                // set cursor at deserid position
  lcd.print(percentValue);                            // print percentValue

  Serial.print("sensor = " );                         // print the results to the serial monitor:
  Serial.print(sensorValue);
  Serial.print("\t output = ");
  Serial.print(outputValue);
  Serial.print("\t procent = ");
  Serial.println(percentValue);

  delay(1000);                                        // set delay
}

void leadingZeros( int value, int width) {            // display result with leading characters
  char valueStr[6];                                   // large enough to hold an int
  itoa (value, valueStr, 10);                         // itoa converts int to string
  int len = strlen(valueStr);                         // calculate length of valueStr
  if (len < width) {
    len = width - len;
    while (len--)
      lcd.print(' ');                                 // for leading zeros place '0' between (), for leading spaces place ' ' between ()
  }
  lcd.print(valueStr);
}
